# Fritzing sketch attenuator (saved by Fritzing 1.0.2b)
breadboards: 1

parts:
  R4 = Resistor [tolerance=±5% power=0.25W resistance=68k package=THT]
  VM4 = Multimeter (DC Voltage)
  R3 = Resistor [tolerance=±5% power=0.25W resistance=18k package=THT]
  C2 = Electrolytic Capacitor [capacitance=10µF voltage=35V package="100 mil [THT, electrolytic]"]
  Channel+1 = DC Power [voltage=0.75V]
  C3 = Ceramic Capacitor [capacitance=0.47µF voltage=35V package="100 mil [THT, multilayer]"]

nets:
  N1: R4.Pin_0, R3.Pin_1, C3.0
  GND: R4.Pin_1, VM4.COM_Probe, C2.-, Channel+1.V-
  N2: VM4.V_Probe, C3.1
  N3: R3.Pin_0, C2.+, Channel+1.V+
