# Fritzing sketch summing_ateenuator (saved by Fritzing 1.0.2b)

parts:
  V1 = DC Power [voltage=0.75V]
  V2 = DC Power [voltage=0.75V]
  R1 = Resistor [tolerance=±5% power=0.25W resistance=260 package=THT]
  R2 = Resistor [tolerance=±5% power=0.25W resistance=260 package=THT]
  R3 = Resistor [tolerance=±5% power=0.25W resistance=820 package=THT]
  VM1 = Multimeter (DC Voltage)
  R5 = Resistor [tolerance=±5% power=0.25W resistance=18k package=THT]
  R6 = Resistor [tolerance=±5% power=0.25W resistance=68k package=THT]
  C4 = Electrolytic Capacitor [capacitance=10µF voltage=35V package="100 mil [THT, electrolytic]"]
  C5 = Ceramic Capacitor [capacitance=0.47µF voltage=35V package="100 mil [THT, multilayer]"]
  VM2 = Multimeter (DC Voltage)

nets:
  N1: V1.V+, R1.Pin_0
  GND: V1.V-, V2.V-, VM1.COM_Probe, R6.Pin_1, C4.-, VM2.COM_Probe
  N2: V2.V+, R2.Pin_0
  N3: R1.Pin_1, R2.Pin_1, R3.Pin_0
  N4: R3.Pin_1, VM1.V_Probe, R5.Pin_0, C4.+
  N5: R5.Pin_1, R6.Pin_0, C5.0
  N6: C5.1, VM2.V_Probe
